# Fritzing sketch Fritzing Circuit (saved by Fritzing 0.9.3b)
circuit board: 8.46667cm x 5.64444cm
breadboards: 1

parts:
  Q3 = Basic FET N-Channel [package="D2Pak [SMD]"]
  Part1 = Arduino Uno (Rev3)
  Q2 = Basic FET N-Channel [package="D2Pak [SMD]"]
  R2 = Resistor [tolerance=±5% resistance=10k package="0805 [SMD]"]
  R1 = Resistor [tolerance=±5% resistance=10k package="0805 [SMD]"]
  A1 = RGB Strip LED
  Q4 = Basic FET N-Channel [package="D2Pak [SMD]"]
  R3 = Resistor [tolerance=±5% resistance=10k package="0805 [SMD]"]
  R4 = Resistor [tolerance=±5% resistance=10k package="0805 [SMD]"]
  Q5 = Basic FET N-Channel [package="D2Pak [SMD]"]
  R5 = Resistor [tolerance=±5% resistance=10k package="0805 [SMD]"]
  Q6 = Basic FET N-Channel [package="D2Pak [SMD]"]
  R6 = Resistor [tolerance=±5% resistance=10k package="0805 [SMD]"]
  Q7 = Basic FET N-Channel [package="D2Pak [SMD]"]

nets (from the breadboard view):
  N1: Q3.Gate, Part1.D11_PWM/MOSI, R3.Pin_1, R4.Pin_1, Q5.Gate
  N2: Q3.drain, Q2.drain, A1.Common_Connect, A1.Blue_Connect, A1.Red_Connect, A1.Green_Connect, Q4.drain, Q5.drain, Q6.drain, Q7.drain
  N3: Q3.source, Q2.source, R2.Pin_0, R1.Pin_0, Q4.source, R3.Pin_0, R4.Pin_0, Q5.source, R5.Pin_0, Q6.source, R6.Pin_0, Q7.source
  N4: Part1.D9_PWM, Q2.Gate, R1.Pin_1, R6.Pin_1, Q7.Gate
  N5: Part1.D10_PWM/SS, R2.Pin_1, Q4.Gate, R5.Pin_1, Q6.Gate

custom parts:
  RGB Strip LED: A tri-color Strip LED with red, green and blue. Pin order: red - common cathode - blue - green

// code stored in the sketch: UnoLEDBasic.ino

//12v LED strip
#define green 6
#define red 5
#define blue 3

///////SOUND SENSOR/////////////////
#define BUTTON_PIN 2



void setup()
{

  
    pinMode(BUTTON_PIN, INPUT_PULLUP);
    pinMode(LED_BUILTIN, OUTPUT);
    
    Serial.begin (9600);

    analogWrite(blue, 255);
    analogWrite(green, 255);
    analogWrite(red, 255);
    digitalWrite(LED_BUILTIN, HIGH);
    delay(500);
  
    analogWrite(blue, 0);
    analogWrite(green, 0);
    analogWrite(red, 0);
    digitalWrite(LED_BUILTIN, LOW);
    delay(500);

    analogWrite(blue, 255);
    analogWrite(green, 255);
    analogWrite(red, 255);
    digitalWrite(LED_BUILTIN, HIGH);
    delay(500);

    analogWrite(blue, 0);
    analogWrite(green, 0);
    analogWrite(red, 0);
    digitalWrite(LED_BUILTIN, LOW);
    delay(500);

    analogWrite(blue, 255);
    analogWrite(green, 255);
    analogWrite(red, 255);
    digitalWrite(LED_BUILTIN, HIGH);
    delay(500);

    analogWrite(blue, 0);
    analogWrite(green, 0);
    analogWrite(red, 0);
    digitalWrite(LED_BUILTIN, LOW);
    delay(500);
}

void loop(){
	
for (int i=o; i<255; i++){
	analogWrite(blue, i);
  analogWrite(green, i);
  analogWrite(red, i);
  digitalWrite(LED_BUILTIN, HIGH);
	delay(500);
}

for (int j=255; j>0; i--){
	analogWrite(blue, j);
  analogWrite(green, j);
  analogWrite(red, j);
  digitalWrite(LED_BUILTIN, Low);
	delay(500);
}

 
}//end of loop/////////////////////////////////////////////////////////////
